// Digital circuit counter.dig as structural Verilog
module counter (
  input  X,
  output I_0,
  output I_1
);

  Counter #(.Bits(2)) counter_1 (.en(1'b1), .C(X), .clr(1'b0), .out({I_1, I_0}));  // open: ovf
endmodule
